# Fritzing sketch circuitoAdafruitMotorShield (saved by Fritzing 0.9.3b)
breadboards: 1

parts:
  Parte2 = Rotoshield - Motor driver shield for Arduino
  Parte1 = Arduino Uno (Rev3)
  M1 = DC Motor
  M2 = DC Motor
  M3 = DC Motor
  M4 = DC Motor
  VCC1 = 4 x AAA Battery Mount  # not connected
  J1 = Basic Servo
  U2 = HC-SR04 [chip_label=IC package="SIP (Single Inline) [THT]"]
  Part1 = Bluetooth HC-05 Macho

nets:
  N1: Parte2.DIG_2, U2.Echo
  N2: Parte2.DIG_3, Parte1.D3_PWM
  N3: Parte2.DIG_4, Parte1.D4
  N4: Parte2.DIG_5, Parte1.D5_PWM
  N5: Parte2.DIG_6, Parte1.D6_PWM
  N6: Parte2.DIG_7, Parte1.D7
  N7: Parte2.A_IN_4, Part1.RXD
  N8: Parte2.A_IN_5, Part1.TXD
  N9: Parte2.DIG_8, Parte1.D8
  N10: Parte2.DIG_9, J1.pulse
  N11: Parte2.DIG_10, U2.Trig
  N12: Parte2.DIG_11, Parte1.D11_PWM/MOSI
  N13: Parte2.DIG_12, Parte1.D12/MISO
  VCC: Parte2.+5V, J1.vcc, U2.Vcc
  GND: Parte2.GND, J1.gnd, U2.GND
  N14: Parte2.M1-2, M1.pin_2
  N15: Parte2.M1-1, M1.pin_1
  N16: Parte2.M2-2, M2.pin_2
  N17: Parte2.M2-1, M2.pin_1
  N18: Parte2.M3-2, M3.pin_2
  N19: Parte2.M3-1, M3.pin_1
  N20: Parte2.M4-2, M4.pin_2
  N21: Parte2.M4-1, M4.pin_1
  3V3: Parte1.3V3, Part1.VCC
  GND_2: Parte1.GND, Part1.GND

custom parts:
  4 x AAA Battery Mount: A 4 x AAA battery pack (4.8 Volts with recharables)
  HC-SR04: HC-SR04 ultrasound distance sensor
