# Fritzing sketch circuitoL298Shield (saved by Fritzing 0.9.6b)
breadboards: 1

parts:
  Parte1 = Arduino Uno (Rev3)
  M1 = DC Motor  # not connected
  M2 = DC Motor  # not connected
  M3 = DC Motor  # not connected
  M4 = DC Motor  # not connected
  VCC1 = 4 x AAA Battery Mount  # not connected
  U2 = HC-SR04 [chip_label=IC package="SIP (Single Inline) [THT]"]
  Parte2 = Arduino Motor Shield
  BLUEFRUIT1 = Adafruit Bluefruit EZ-LINK v1.0
  J1 = Basic Servo

nets:
  N1: Parte1.D8, Parte2.D8
  N2: Parte1.D9_PWM, Parte2.D9
  N3: Parte1.D10_PWM/SS, Parte2.D10
  N4: Parte1.D11_PWM/MOSI, Parte2.D11
  N5: Parte1.D12/MISO, Parte2.D12
  N6: Parte1.D13/SCK, Parte2.D13
  N7: Parte1.D2, J1.pulse
  N8: Parte1.D3_PWM, U2.Echo
  N9: Parte1.D5_PWM, U2.Trig
  N10: Parte1.D6_PWM, BLUEFRUIT1.RX
  N11: Parte1.D7, BLUEFRUIT1.TX
  3V3: Parte1.3V3, BLUEFRUIT1.Vin
  VCC: Parte1.5V, U2.Vcc, J1.vcc
  GND: Parte1.GND, U2.GND, BLUEFRUIT1.GND, J1.gnd

custom parts:
  4 x AAA Battery Mount: A 4 x AAA battery pack (4.8 Volts with recharables)
  HC-SR04: HC-SR04 ultrasound distance sensor
  Adafruit Bluefruit EZ-LINK v1.0: Bluefruit EZ-LINK, Bluetooth Serial Link & Arduino Programmer
